# Fritzing sketch Scrub_fm (saved by Fritzing 0.9.3b)
circuit board: 8.46667cm x 5.64444cm
breadboards: 1

parts:
  Part1 = Si4713 Stereo FM Transmitter
  Part2 = Arduino Nano (Rev3.0)
  S2 = Pushbutton [package="[SMD]"]
  Part3 = Adafruit Breadboard-Friendly NeoPixel [part_number="Adafruit #1312"]

nets:
  5V: Part1.VIN, Part2.5V, S2.Pin_3, S2.Pin_4, Part3.VDD
  GND: Part1.GND, Part2.GND, Part3.GND
  N1: Part1.SDA, Part2.A4
  N2: Part1.SCL, Part2.A5
  N3: Part1.RST, Part2.D12/MISO
  N4: Part2.D2, S2.Pin_1, S2.Pin_2
  N5: Part2.D6, Part3.IN

custom parts:
  Si4713 Stereo FM Transmitter: Yaaar! Become your very own pirate radio station with this FM radio transmitter. This breakout board, based on the best-of-class Si4713, is an all-in-one stereo audio FM transmitter that can also transmit RDS/RBDS data!
  Adafruit Breadboard-Friendly NeoPixel: This is the easiest way possible to add small, bright RGB pixels to your project. We took the same technology from our Flora NeoPixels and made them breadboard friendly, with two rows of 3 x 0.1" spaced header on each side for easy soldering, chaining and breadboarding. These ultra-bright LEDs have a constant-current driver cooked right into the LED package! The pixels are chainable - so you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
